# Fritzing sketch PinConnections (saved by Fritzing 0.7.10b)

parts:
  Arduino_Ethernet_Shield1 = Arduino Ethernet Shield
  LED1 = RGB LED (com. anode, rbg) [package="5 mm [THT]"]

nets (from the schematic view):
  N1: Arduino_Ethernet_Shield1.GND#1, LED1.common_anode, LED1.blue_cathode
  N2: Arduino_Ethernet_Shield1.+5V, LED1.red_cathode
  N3: Arduino_Ethernet_Shield1.A0, LED1.green_cathode

notes:
  NOTE: In reality, this is not a LED! It is a PIR sensor!
  cable colors in order from left to right:
  red, black, black, yellow
